# Fritzing sketch Relay Board for EL Wire (saved by Fritzing 0.9.3b)
breadboards: 1

parts:
  PSU_12V = Battery
  3V_SPDT_Relay_(1) = RELAY [package=relay-t9a]
  Micro_Bit_GPIO = Screw terminal - 2 pins [package=THT]
  12V_Inverter_(1) = IC, DIP package, 4 pins [chip_label=Inverter]
  3V_SPDT_Relay_(2) = RELAY [package=relay-t9a]
  3V_SPDT_Relay_(3) = RELAY [package=relay-t9a]
  3V_SPDT_Relay_(4) = RELAY [package=relay-t9a]
  3V_SPDT_Relay_(5) = RELAY [package=relay-t9a]
  3V_SPDT_Relay_(6) = RELAY [package=relay-t9a]
  12V_Inverter_(2) = IC, DIP package, 4 pins [chip_label=Inverter]
  12V_Inverter_(3) = IC, DIP package, 4 pins [chip_label=Inverter]
  12V_Inverter_(4) = IC, DIP package, 4 pins [chip_label=Inverter]
  12V_Inverter_(5) = IC, DIP package, 4 pins [chip_label=Inverter]
  12V_Inverter_(6) = IC, DIP package, 4 pins [chip_label=Inverter]
  Micro_Bit_GPIO_2 = Screw terminal - 2 pins [package=THT]
  Micro_Bit_GPIO_3 = Screw terminal - 2 pins [package=THT]
  Micro_Bit_GPIO_4 = Screw terminal - 2 pins [package=THT]
  Micro_Bit_GPIO_5 = Screw terminal - 2 pins [package=THT]
  Micro_Bit_GPIO_6 = Screw terminal - 2 pins [package=THT]

nets:
  N1: PSU_12V.-, 12V_Inverter_(1).pin2, 12V_Inverter_(2).pin2, 12V_Inverter_(3).pin2, 12V_Inverter_(4).pin2, 12V_Inverter_(5).pin2, 12V_Inverter_(6).pin2
  N2: PSU_12V.+, 3V_SPDT_Relay_(1).MAIN, 3V_SPDT_Relay_(2).MAIN, 3V_SPDT_Relay_(3).MAIN, 3V_SPDT_Relay_(4).MAIN, 3V_SPDT_Relay_(5).MAIN, 3V_SPDT_Relay_(6).MAIN
  N3: 3V_SPDT_Relay_(1).COIL1, Micro_Bit_GPIO.pin2
  N4: 3V_SPDT_Relay_(1).COIL2, Micro_Bit_GPIO.pin1
  N5: 3V_SPDT_Relay_(1).NO, 12V_Inverter_(1).pin1
  N6: 3V_SPDT_Relay_(2).COIL1, Micro_Bit_GPIO_2.pin2
  N7: 3V_SPDT_Relay_(2).COIL2, Micro_Bit_GPIO_2.pin1
  N8: 3V_SPDT_Relay_(2).NO, 12V_Inverter_(2).pin1
  N9: 3V_SPDT_Relay_(3).COIL1, Micro_Bit_GPIO_3.pin2
  N10: 3V_SPDT_Relay_(3).COIL2, Micro_Bit_GPIO_3.pin1
  N11: 3V_SPDT_Relay_(3).NO, 12V_Inverter_(3).pin1
  N12: 3V_SPDT_Relay_(4).COIL1, Micro_Bit_GPIO_4.pin2
  N13: 3V_SPDT_Relay_(4).COIL2, Micro_Bit_GPIO_4.pin1
  N14: 3V_SPDT_Relay_(4).NO, 12V_Inverter_(4).pin1
  N15: 3V_SPDT_Relay_(5).COIL1, Micro_Bit_GPIO_5.pin2
  N16: 3V_SPDT_Relay_(5).COIL2, Micro_Bit_GPIO_5.pin1
  N17: 3V_SPDT_Relay_(5).NO, 12V_Inverter_(5).pin1
  N18: 3V_SPDT_Relay_(6).COIL1, Micro_Bit_GPIO_6.pin2
  N19: 3V_SPDT_Relay_(6).COIL2, Micro_Bit_GPIO_6.pin1
  N20: 3V_SPDT_Relay_(6).NO, 12V_Inverter_(6).pin1
